// Logisim project pj.circ as structural Verilog: 1 circuit, main circuit main
module main (
  output [7:0] OP2,
  output [7:0] OP1
);

  wire [7:0] A_out, B_out, C_out, D_out, or_1_out;

  assign A_out = OP1 & OP1;  // AND_Gate A, 8 bits wide
  assign B_out = OP2 & OP2;  // AND_Gate B, 8 bits wide
  assign C_out = OP1 & OP1;  // AND_Gate C, 8 bits wide
  assign D_out = OP2 & OP2;  // AND_Gate D, 8 bits wide
  assign or_1_out = A_out | B_out | C_out | D_out;  // OR_Gate or_1, 8 bits wide
endmodule
